# Fritzing sketch FRITZING (saved by Fritzing 0.9.3b)
breadboards: 1

parts:
  U1 = 74HC595 [package="DIP16 [THT]"]
  U2 = 74HC595 [package="DIP16 [THT]"]
  DI1 = 7-Segment LED Display [package=THT]
  R1 = Resistor [tolerance=±5% resistance=220 package=THT]
  S1 = Pushbutton [package="[SMD]"]
  S2 = Pushbutton [package="[SMD]"]
  S3 = Pushbutton [package="[SMD]"]
  R2 = Resistor [tolerance=±5% resistance=10k package=THT]
  R3 = Resistor [tolerance=±5% resistance=10k package=THT]
  R4 = Resistor [tolerance=±5% resistance=10k package=THT]
  LED1 = LED - 5mm [color="Red (633nm)" package="5 mm [THT]"]
  LED2 = LED - 5mm [color="Yellow (585nm)" package="5 mm [THT]"]
  LED4 = LED - 5mm [color="Red (633nm)" package="5 mm [THT]"]
  LED7 = LED - 5mm [color="Yellow (585nm)" package="5 mm [THT]"]
  LED8 = LED - 5mm [color="Green (555nm)" package="5 mm [THT]"]
  LED9 = LED - 5mm [color="Green (555nm)" package="5 mm [THT]"]
  R5 = Resistor [tolerance=±5% resistance=220 package=THT]
  R6 = Resistor [tolerance=±5% resistance=220 package=THT]
  R7 = Resistor [tolerance=±5% resistance=220 package=THT]
  R8 = Resistor [tolerance=±5% resistance=220 package=THT]
  R9 = Resistor [tolerance=±5% resistance=220 package=THT]
  R10 = Resistor [tolerance=±5% resistance=220 package=THT]
  J1 = Piezo Speaker
  R11 = Resistor [tolerance=±5% resistance=220 package=THT]
  Part1 = Arduino Uno (Rev3)
  C1 = Electrolytic Capacitor [capacitance=1µF package="100 mil [THT, electrolytic]"]  # not connected
  R12 = Photocell (LDR) [package=THT]
  R13 = Resistor [tolerance=±5% resistance=330k package=THT]
  J2 = Basic Servo

nets:
  N1: U1.Q1, DI1.cathodeB
  N2: U1.Q2, DI1.cathodeC
  N3: U1.Q3, DI1.cathodeD
  N4: U1.Q4, DI1.cathodeE
  N5: U1.Q5, DI1.cathodeF
  N6: U1.Q6, DI1.cathodeG
  GND: U1.GND, U1.OE, U2.GND, U2.OE, R1.Pin_0, S1.Pin_1, S1.Pin_2, S2.Pin_1, S2.Pin_2, S3.Pin_1, S3.Pin_2, LED1.anode, LED2.anode, LED4.anode, LED8.anode, LED9.anode, J1.pin1, Part1.GND, R13.Pin_0, J2.gnd
  VCC: U1.MR, U1.VCC, U2.MR, U2.VCC, R2.Pin_1, R3.Pin_1, R4.Pin_1, Part1.5V, R12.pin_0, J2.vcc
  N7: U1.SH_CP, Part1.D12/MISO
  N8: U1.ST_CP, U2.ST_CP, Part1.D9_PWM
  N9: U1.DS, U2.DS, Part1.D10_PWM/SS
  N10: U1.Q0, DI1.cathodeA
  N11: U2.Q2, R6.Pin_1
  N12: U2.Q3, R7.Pin_1
  N13: U2.Q4, R8.Pin_1
  N14: U2.Q5, R9.Pin_1
  N15: U2.Q6, R10.Pin_1
  N16: U2.SH_CP, Part1.D11_PWM/MOSI
  N17: U2.Q0, R5.Pin_1
  N18: DI1.commAnode#7, R1.Pin_1
  N19: S1.Pin_3, S1.Pin_4, R2.Pin_0, Part1.D7
  N20: S2.Pin_3, S2.Pin_4, R3.Pin_0, Part1.D6_PWM
  N21: S3.Pin_3, S3.Pin_4, R4.Pin_0, Part1.D5_PWM
  N22: LED1.cathode, R5.Pin_0
  N23: LED2.cathode, R6.Pin_0
  N24: LED4.cathode, R8.Pin_0
  N25: LED7.cathode, R9.Pin_0
  N26: LED8.cathode, R7.Pin_0
  N27: LED9.cathode, R10.Pin_0
  N28: J1.pin2, R11.Pin_1
  N29: R11.Pin_0, Part1.D8
  N30: Part1.A0, R12.pin_1, R13.Pin_1
  N31: Part1.D3_PWM, J2.pulse
